# Fritzing sketch Schema-circuit (saved by Fritzing 0.9.3b)
breadboards: 1

parts:
  부품3 = FC-28 Soil Hygrometer Module
  부품4 = FC-28 Soil Hygrometer Module - Probe
  R1 = PHOTOCELL [package=photocell]
  DHT1 = DHT11 Humitidy and Temperature Sensor (3 pins)
  R2 = Resistor [tolerance=±5% resistance=220 package="0805 [SMD]"]
  Part1 = Arduino Uno (Rev3)
  M1 = ESP-01 Breakout Board Breadboard Adapter [part_number=ESP8266]

nets:
  N1: 부품3.POS, 부품4.POS
  N2: 부품3.NEG, 부품4.NEG
  N3: R1.P$1, R2.Pin_1, Part1.A1
  VDD: R1.P$2, DHT1.VDD, Part1.5V, M1.VCC
  N4: DHT1.DATA, Part1.D11_PWM/MOSI
  GND: DHT1.GND, R2.Pin_0, Part1.GND, M1.GND
  N5: Part1.D2, M1.TXD
  N6: Part1.D3_PWM, M1.RXD

custom parts:
  FC-28 Soil Hygrometer Module: The FC-28 is a soil hygrometer module that uses the Texas Instruments LM393 comparator chip to provide an analog measurement of soil humidity. The digital output is high when soil moisture is over a certain threshold, as determined by adjusting the potentiometer.
  FC-28 Soil Hygrometer Module - Probe: The FC-28 is a soil hygrometer module that uses the Texas Instruments LM393 comparator chip to provide an analog measurement of soil humidity.
  DHT11 Humitidy and Temperature Sensor (3 pins): DHT11 Humidity and Temperature Sensor (3 pins) from the design created by John De Cristofaro for Adafruit Industries.
  ESP-01 Breakout Board Breadboard Adapter: Generic WiFi Module based on the ESP8266 with onboard PCB antenna and UART communications with breadboard friendly breakout board attached.

// code stored in the sketch: Code-circuit.ino
#include <ESP8266WiFi.h>
#include "DHT.h"

#define DHTPIN D6     // what digital pin we're connected to
#define LIGHT A1      // luminosity sensor
#define MOISTURE D7   // soil moisture

#define DHTTYPE DHT11  

// Wi-Fi Settings
const char* ssid = "Ionica"; 
const char* password = "ioana123"; 

DHT dht(DHTPIN, DHTTYPE);

WiFiClient client;

// ThingSpeak Settings
const int channelID = 1714134;
String writeAPIKey = "RHI038IPL0EGGXB0"; 
const char* server = "api.thingspeak.com";
const int postingInterval = 600 * 1000; // post data every x seconds

void setup() {
  dht.begin();   
  WiFi.begin(ssid, password);

  while (WiFi.status() != WL_CONNECTED) {
    delay(500);
  }
}

void loop() {  
  if (client.connect(server, 80)) {
    float h = dht.readHumidity(); // air humidity
    float t = dht.readTemperature(); // air temperature
    int l = analogRead(LIGHT);      // luminosity
    // int m = ( 100 - ( (digitalRead(MOISTURE)/1023.00) * 100 ) ); // moisture as percentage
    int m = digitalRead(MOISTURE);

    // Construct API request body
    String body = "&field1=";
           body += String(t);
           body += "&field2=";
           body += String(h);
           body += "&field3=";
           body += String(l);
           body += "&field4=";
           body += String(m);
           
    client.println("POST /update HTTP/1.1");
    client.println("Host: api.thingspeak.com");
    client.println("User-Agent: ESP8266 (nothans)/1.0");
    client.println("Connection: close");
    client.println("X-THINGSPEAKAPIKEY: " + writeAPIKey);
    client.println("Content-Type: application/x-www-form-urlencoded");
    client.println("Content-Length: " + String(body.length()));
    client.println("");
    client.print(body);
  }
  client.stop();


  // wait and then post again
  delay(postingInterval);
}
